# Fritzing sketch PORmkII (saved by Fritzing 0.9.4)
breadboards: 1

parts:
  U1 = ESP32S-HiLetgo [part_number=ESP32S-HiLetgo]
  LCD1 = 2.8" SPI TFT Module [part_number=MSP2807]
  C1 = Electrolytic Capacitor [capacitance=10µF package="100 mil [THT, electrolytic]"]
  DS1 = DS18B20 1-Wire Temperature Sensor [part_number=DS18B20]
  R1 = Resistor [tolerance=±5% resistance=4.7k package=THT]
  J1 = Screw terminal - 2 pins [package=THT]

nets:
  N1: U1.3.3, LCD1.pin1, LCD1.pin4, LCD1.pin8, C1.+, DS1.VDD, R1.Pin_1
  GND: U1.GND, LCD1.pin2, C1.-, DS1.GND, J1.pin2
  N2: U1.VIN, J1.pin1
  N3: U1.GPIO15, LCD1.pin3
  N4: U1.GPIO2, LCD1.pin5
  N5: U1.GPIO18, LCD1.pin7, LCD1.pin10
  N6: U1.GPIO19, LCD1.pin9, LCD1.pin13
  N7: U1.GPIO21, LCD1.pin11
  N8: U1.GPIO22, DS1.DQ, R1.Pin_0
  N9: U1.GPIO23, LCD1.pin6, LCD1.pin12

custom parts:
  ESP32S-HiLetgo: HiLetgo ESP-WROOM-32 ESP32 ESP-32S Development Board 2.4GHz Dual-Mode WiFi + Bluetooth Dual Cores Microcontroller The ESP32 integrated with Antenna switches, RF Balun, power amplifiers, low-noise amplifiers, filters, and management modules, and the entire solution occupies the least area of PCB. 2.4 GHz Wi-Fi plus Bluetooth dual-mode chip, with TSMC Ultra-low power consumption 40nm technology,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
  2.8" SPI TFT Module: A generic 2.8 inch LCD TFT 320x240 display with touchscreen and SD card slot. Uses the ILI9341 controller, like the Adafruit displays of this size uses.
